// Logisim project proyecto.circ as structural Verilog: 1 circuit, main circuit main
module main (
  input  A,
  input  B,
  input  C,
  input  D,
  input  in_5,
  input  E,
  input  in_7,
  input  in_8,
  input  in_9,
  input  _257,
  input  _258,
  input  in_12,
  input  _259,
  input  in_14,
  input  _261,
  input  in_16,
  input  _262,
  input  in_18,
  input  in_19,
  input  in_20,
  output [3:0] out_21,
  output [2:0] out_22,
  output [3:0] out_23,
  output [2:0] out_24
);

  wire and_1_out, and_2_out, clock_1_out, multiplexer_1_out, not_1_out;
  wire [3:0] counter_1_q, undriven, undriven_2;
  wire [8:3] multiplexer_3_out;

  or or_1 (out_23[3], A, B, C, D, E, and_1_out);
  and and_1 (and_1_out, not_1_out, and_2_out);
  and and_2 (and_2_out, out_22[2], out_22[1]);
  ROM #(.addrWidth(4), .dataWidth(4)) rom_1 (.addr({out_23[3], out_22}), .data(out_21));
  Multiplexer #(.select(3)) multiplexer_1 (
    .in0(_257), .in1(_258), .in2(_259), .in3(_261), .in4(_262), .in5(in_19), .out(multiplexer_1_out),
    .sel(out_22));  // open: in6, in7
  Clock clock_1 (.out(clock_1_out));
  not not_1 (not_1_out, out_22[0]);
  Counter #(.max('hf), .width(4)) counter_1 (
    .load(out_23[3]), .up(1'b1), .count(multiplexer_1_out), .clk(clock_1_out), .D(out_21), .Q(counter_1_q));  // open: clr, carry
  Multiplexer #(.select(4), .width(4)) multiplexer_2 (
    .in8(undriven), .in14(undriven_2));  // open: in0, in1, in2, in3, in4, in5, in6, in7, in9, in10, in11, in12, in13, in15, out, sel
  Multiplexer #(.select(4), .width(9)) multiplexer_3 (
    .in0(9'h100), .in1(9'h101), .in2(9'h102), .in3(9'h103), .in4(9'h104), .in5(9'h105), .in6(9'h106),
    .out({multiplexer_3_out, out_22}), .sel(counter_1_q));  // open: in7, in8, in9, in10, in11, in12, in13, in14, in15

  assign out_23[2:0] = out_22;
  assign out_24 = out_22;

  // Notes on the sheet:
  //   260
  //   contents of rom_1 (hex, n*v repeats v):
  //   8*0 4
endmodule
